# Fritzing sketch MashedPixels-autoreboot (saved by Fritzing 0.8.7b)
circuit board: 1.82984cm x 3.06555cm
breadboards: 1

parts:
  Composant1 = Arduino Pro Mini v13
  Composant2 = FTDI Basic Programmer
  J1 = Power Jack [package=power_jack_combo]
  S1 = Pushbutton [package="[THT]"]
  U1 = 3.5mm Audio Jack [package=audio-jack]

nets:
  N1: Composant1.DTR, Composant2.DTR
  N2: Composant1.D0/TX, Composant2.RXI
  N3: Composant1.D1/RX, Composant2.TXO
  N4: Composant1.VCC, Composant2.POWER
  GND: Composant1.GND, Composant2.CTS, Composant2.GND, J1.GND, S1.Pin_3, S1.Pin_4
  N5: Composant1.RAW, J1.PWR, U1.RIGHT
  N6: Composant1.D10_PWM/SS, S1.Pin_1, S1.Pin_2
  N7: Composant1.D3_PWM, U1.LEFT
