# Fritzing sketch MashedPixels (saved by Fritzing 0.8.7b)
circuit board: 2.00531cm x 6.2681cm
breadboards: 1

parts:
  Arduino1 = Arduino Pro Mini v13
  R1 = Resistor [tolerance=±5% resistance=510k package=THT]
  C1 = Ceramic Capacitor [capacitance=100nF package="100 mil [THT, multilayer]"]
  FTDI = FTDI Basic Programmer
  Power = Power Jack [package=power_jack_combo]
  Action = Pushbutton [package="[THT]"]
  LED_Strip = 3.5mm Audio Jack [package=audio-jack-3.5mm-smd]

nets:
  N1: Arduino1.DTR, FTDI.DTR
  N2: Arduino1.D0/TX, FTDI.RXI
  N3: Arduino1.D1/RX, FTDI.TXO
  N4: Arduino1.VCC, R1.Pin_1, C1.1, FTDI.POWER
  GND: Arduino1.GND, FTDI.CTS, FTDI.GND, Power.GND, Action.Pin_1, Action.Pin_2, LED_Strip.SLEEVE
  N5: Arduino1.RAW, Power.PWR, LED_Strip.LEFT
  N6: Arduino1.RESET, Arduino1.A3, R1.Pin_0, C1.0
  N7: Arduino1.D9_PWM, LED_Strip.RIGHT
  N8: Arduino1.D2, Action.Pin_3, Action.Pin_4

notes:
  Mashed Pixels
  V1.0 by Alexis ISAAC
